# Fritzing sketch IF4000_Proyecto_Jesner_Alisson (saved by Fritzing 0.9.3b)
breadboards: 2

parts:
  XTAL_(4_Mhz) = Crystal [frequency="16 Mhz" package=THT]
  Regulador_de_Voltaje = Voltage Regulator - 5V [package="TO220 [THT]"]
  Pulsador_Izquierda = Momentary Switch [package=ksa_sealed_tac_switch]
  PIC_16F84A = PIC 16F8x [package=ssop20]
  Batería = Battery block 9V
  LED = LED - 5mm [color="Red (633nm)" package="5 mm [THT]"]
  Capacitor = Electrolytic Capacitor [capacitance=1µF package="100 mil [THT, electrolytic]"]
  Capacitor_2 = Tantalum Capacitor [capacitance=1μF package="100 mil [THT, tantalum]"]
  R1 = Resistor [tolerance=±5% resistance=220 package=THT]
  U7 = L298_BRIDGE_DRIVER [package=powerso20]
  Pulsador_Derecha = Momentary Switch [package=ksa_sealed_tac_switch]
  Pulsador_Atrás = Momentary Switch [package=ksa_sealed_tac_switch]
  Pulsador_Adelante = Momentary Switch [package=ksa_sealed_tac_switch]
  Pulsador_Detener = Momentary Switch [package=ksa_sealed_tac_switch]
  Pulsador_Comenzar = Momentary Switch [package=ksa_sealed_tac_switch]
  R2 = Resistor [tolerance=±5% resistance=220 package=THT]
  R3 = Resistor [tolerance=±5% resistance=220 package=THT]
  R4 = Resistor [tolerance=±5% resistance=220 package=THT]
  R5 = Resistor [tolerance=±5% resistance=220 package=THT]
  R6 = Resistor [tolerance=±5% resistance=220 package=THT]
  R7 = Resistor [tolerance=±5% resistance=220 package=THT]
  DC_MOTOR_1 = DC Motor
  DC_MOTOR_2 = DC Motor
  Capacitor_3 = Tantalum Capacitor [capacitance="1 μF" package="C 6032 [SMD, tantalum]"]
  Pulsador_MCLR = Momentary Switch [package=ksa_sealed_tac_switch]

nets:
  N1: XTAL_(4_Mhz).pin_0, PIC_16F84A.RA7_OSC1, Capacitor_2.-
  N2: XTAL_(4_Mhz).pin_1, PIC_16F84A.RA6_OSC2, Capacitor_3.-
  N3: Regulador_de_Voltaje.input_voltage, Regulador_de_Voltaje.output_voltage, Batería.+, Capacitor.-, Capacitor_2.+, U7.VS, R4.Pin_0, Capacitor_3.+, Pulsador_MCLR.1
  GND: Regulador_de_Voltaje.GND, PIC_16F84A.VSS, Batería.-, LED.anode, Capacitor.+, U7.GND
  N4: Pulsador_Izquierda.1, PIC_16F84A.RA3_AN3, R5.Pin_1
  N5: Pulsador_Izquierda.3, Pulsador_Derecha.3, Pulsador_Atrás.3, Pulsador_Adelante.3, Pulsador_Detener.3, Pulsador_Comenzar.3
  N6: PIC_16F84A.RA2_AN2, Pulsador_Atrás.1, R2.Pin_1
  N7: PIC_16F84A.RA4_AN4, R1.Pin_1, Pulsador_Derecha.1
  N8: PIC_16F84A.RA5_MCLR, R4.Pin_1
  N9: PIC_16F84A.RB1_SDA, Pulsador_Comenzar.1, R3.Pin_1
  N10: PIC_16F84A.RB2_RX, U7.IN2
  N11: PIC_16F84A.RB3, U7.IN1
  N12: PIC_16F84A.RB4_SCL, U7.IN3
  N13: PIC_16F84A.RB5_TX, U7.ENB
  N14: PIC_16F84A.RB6_PGC, LED.cathode
  N15: PIC_16F84A.RA0_AN0, Pulsador_Adelante.1, R6.Pin_1
  N16: PIC_16F84A.RA1_AN1, Pulsador_Detener.1, R7.Pin_1
  N17: R1.Pin_0, R2.Pin_0, R3.Pin_0, R5.Pin_0, R6.Pin_0, R7.Pin_0
  N18: U7.OUT1, DC_MOTOR_2.pin_1
  N19: U7.OUT2, DC_MOTOR_2.pin_2
  N20: U7.OUT3, DC_MOTOR_1.pin_2
  N21: U7.OUT4, DC_MOTOR_1.pin_1
